// Digital circuit 8-Bit_AdderOneCompliment.dig as structural Verilog
module _8_Bit_AdderOneCompliment (
  input  [7:0] A_In,
  input  [7:0] B_In,
  input  Carry_In,
  input  SUB,
  input  SUB_2,
  input  Over_Underflow,
  output [7:0] Sum_Out
);

  wire full_adder_1_p1, full_adder_1_p3, full_adder_1_p4, full_adder_2_p1, full_adder_2_p4, full_adder_3_p1,
       full_adder_3_p4, full_adder_4_p1, full_adder_4_p4, full_adder_5_p1, full_adder_5_p4, full_adder_6_p1,
       full_adder_6_p4, full_adder_7_p1, full_adder_7_p4, full_adder_8_p1;

  xor xor_1 (Over_Underflow, SUB_2, full_adder_1_p3);
  // Full_Adder full_adder_1: pin names not known; wires that end beside it: full_adder_1_p1, A_In[7], full_adder_1_p3, full_adder_1_p4, Sum_Out[7]
  // Full_Adder full_adder_2: pin names not known; wires that end beside it: full_adder_2_p1, A_In[6], full_adder_1_p4, full_adder_2_p4, Sum_Out[6]
  // Full_Adder full_adder_3: pin names not known; wires that end beside it: full_adder_3_p1, A_In[5], full_adder_2_p4, full_adder_3_p4, Sum_Out[5]
  // Full_Adder full_adder_4: pin names not known; wires that end beside it: full_adder_4_p1, A_In[4], full_adder_3_p4, full_adder_4_p4, Sum_Out[4]
  // Full_Adder full_adder_5: pin names not known; wires that end beside it: full_adder_5_p1, A_In[3], full_adder_4_p4, full_adder_5_p4, Sum_Out[3]
  xor xor_2 (full_adder_1_p1, B_In[7], SUB);
  // Full_Adder full_adder_6: pin names not known; wires that end beside it: full_adder_6_p1, A_In[2], full_adder_5_p4, full_adder_6_p4, Sum_Out[2]
  xor xor_3 (full_adder_2_p1, B_In[6], SUB);
  // Full_Adder full_adder_7: pin names not known; wires that end beside it: full_adder_7_p1, A_In[1], full_adder_6_p4, full_adder_7_p4, Sum_Out[1]
  xor xor_4 (full_adder_3_p1, B_In[5], SUB);
  // Full_Adder full_adder_8: pin names not known; wires that end beside it: full_adder_8_p1, A_In[0], full_adder_7_p4, Carry_In, Sum_Out[0]
  xor xor_5 (full_adder_4_p1, B_In[4], SUB);
  xor xor_6 (full_adder_5_p1, B_In[3], SUB);
  xor xor_7 (full_adder_6_p1, B_In[2], SUB);
  xor xor_8 (full_adder_7_p1, B_In[1], SUB);
  xor xor_9 (full_adder_8_p1, B_In[0], SUB);
endmodule
