// Digital circuit Full-Adder.dig as structural Verilog
module Full_Adder (
  input  Carry_In,
  input  A_In,
  input  B_In,
  output Carry_Out,
  output Sum_Out
);

  wire half_adder_1_carry_out, half_adder_1_sum_out, half_adder_2_carry_out;

  Half_Adder half_adder_1 (
    .A_In(A_In), .B_In(B_In), .Sum_Out(half_adder_1_sum_out), .Carry_Out(half_adder_1_carry_out));
  Half_Adder half_adder_2 (
    .A_In(Carry_In), .B_In(half_adder_1_sum_out), .Sum_Out(Sum_Out), .Carry_Out(half_adder_2_carry_out));
  or or_1 (Carry_Out, half_adder_2_carry_out, half_adder_1_carry_out);
endmodule
