// Digital circuit 8-Bit_Adder.dig as structural Verilog
module _8_Bit_Adder (
  input  [7:0] A_In,
  input  [7:0] B_In,
  input  Carry_In,
  output [7:0] Sum_Out,
  output Carry_Out
);

  wire full_adder_1_p4, full_adder_2_p4, full_adder_3_p4, full_adder_4_p4, full_adder_5_p4, full_adder_6_p4,
       full_adder_7_p4;

  // Full_Adder full_adder_1: pin names not known; wires that end beside it: B_In[7], A_In[7], Carry_Out, full_adder_1_p4, Sum_Out[7]
  // Full_Adder full_adder_2: pin names not known; wires that end beside it: B_In[6], A_In[6], full_adder_1_p4, full_adder_2_p4, Sum_Out[6]
  // Full_Adder full_adder_3: pin names not known; wires that end beside it: B_In[5], A_In[5], full_adder_2_p4, full_adder_3_p4, Sum_Out[5]
  // Full_Adder full_adder_4: pin names not known; wires that end beside it: B_In[4], A_In[4], full_adder_3_p4, full_adder_4_p4, Sum_Out[4]
  // Full_Adder full_adder_5: pin names not known; wires that end beside it: B_In[3], A_In[3], full_adder_4_p4, full_adder_5_p4, Sum_Out[3]
  // Full_Adder full_adder_6: pin names not known; wires that end beside it: B_In[2], A_In[2], full_adder_5_p4, full_adder_6_p4, Sum_Out[2]
  // Full_Adder full_adder_7: pin names not known; wires that end beside it: B_In[1], A_In[1], full_adder_6_p4, full_adder_7_p4, Sum_Out[1]
  // Full_Adder full_adder_8: pin names not known; wires that end beside it: B_In[0], A_In[0], full_adder_7_p4, Carry_In, Sum_Out[0]
endmodule
